# Fritzing sketch slumpen (saved by Fritzing 0.9.2b)
breadboards: 1

parts:
  Part1 = Arduino Leonardo (Rev3b)
  LED1 = LED - 5mm [color="Red (633nm)" package="5 mm [THT]"]
  LED2 = LED - 5mm [color="Red (633nm)" package="5 mm [THT]"]
  LED3 = LED - 5mm [color="Red (633nm)" package="5 mm [THT]"]
  LED5 = LED - 5mm [color="Red (633nm)" package="5 mm [THT]"]
  LED6 = LED - 5mm [color="Red (633nm)" package="5 mm [THT]"]
  LED4 = LED - 5mm [color="Red (635nm)" package="5 mm [THT]"]
  R1 = Resistor [tolerance=±5% resistance=220 package=THT]
  S1 = Pushbutton [package=THT]

nets:
  N1: Part1.D2/SDA, LED6.anode
  N2: Part1.D3_PWM/SCL, LED5.anode
  N3: Part1.D4/A6, LED4.anode
  N4: Part1.D5_PWM, LED3.anode
  N5: Part1.D6_PWM/A7, LED2.anode
  N6: Part1.D7, LED1.anode
  N7: Part1.D8/A8, S1.leg1
  N8: Part1.GND, R1.Pin_0, S1.leg0
  N9: LED1.cathode, LED2.cathode, LED3.cathode, LED5.cathode, LED6.cathode, LED4.cathode, R1.Pin_1
